// Logisim project jaw280.circ as structural Verilog: 6 circuits, main circuit main
module main (
);

  wire alu_neg, alu_zero, clear, clk, clock_1_out, ctrl_dec7, ctrl_inc7, dec7, display_enable, fl_update,
       halt, i_type, inc7, jr_ctrl, kbd_enable, MultSrc, neg_out, pc_dec7, pc_inc7, prod_en, ram_enable,
       ram_enable_ctrl, ram_src, ram_src_ctrl, ram_src_pc, reg_en, ret_cmd, ret_ctrl, scr_enable, zero_out;
  wire [1:0] ALUSrcB;
  wire [2:0] alu_oper, rd, rs, rs_ctrl, rt;
  wire [3:0] DataSrc, display_unit_1_digit_1, display_unit_1_digit_2, display_unit_1_digit_3,
       display_unit_1_digit_4, pc_op;
  wire [6:0] kbd_out;
  wire [7:0] imm, lui_data;
  wire [15:0] adder_1_out, alu_high, alu_inB, alu_out, bit_extender_1_out, data_in, mfhi_out, mflo_out,
       pc_output, ram_in, ram_out, ram_val, rom_out, rt_out, subtractor_1_out, sxt_imm, zxt_imm;
  wire [15:8] rs_out;
  wire [31:0] bit_extender_4_out, mult_and_acc, prod_in;

  Clock clock_1 (.out(clock_1_out));
  assign bit_extender_1_out = {{9{1'b0}}, kbd_out};  // Bit_Extender bit_extender_1
  and and_1 (clk, clock_1_out, ~halt);  // AND_Gate
  LED u_Halt (.in(halt));
  assign zxt_imm = {{8{1'b0}}, imm};  // Bit_Extender bit_extender_2
  assign sxt_imm = {{8{imm[7]}}, imm};  // Bit_Extender bit_extender_3
  Multiplexer #(.select(4), .width(16), .enable("false")) multiplexer_1 (
    .in1(zxt_imm), .in2({imm, lui_data}), .in3({rs_out, lui_data}), .in4(mfhi_out), .in5(mflo_out),
    .in6(ram_out), .in7(alu_out), .in8(bit_extender_1_out), .out(data_in), .sel(DataSrc));  // open: in0, in9, in10, in11, in12, in13, in14, in15
  // Probe on DataSrc
  Hex_Digit_Display hex_digit_display_1 (.value(display_unit_1_digit_2));  // open: dp
  Hex_Digit_Display hex_digit_display_2 (.value(display_unit_1_digit_1));  // open: dp
  display_unit display_unit_1 (
    .Clock(clk), .Clear(clear), .Write_Enable(display_enable), .Data({rs_out, lui_data}),
    .Digit_1(display_unit_1_digit_1), .Digit_2(display_unit_1_digit_2), .Digit_3(display_unit_1_digit_3),
    .Digit_4(display_unit_1_digit_4));
  Keyboard keyboard_1 (.clk(clk), .re(kbd_enable), .data(kbd_out));  // open: clr, avail
  // Probe on data_in
  or or_1 (ram_src, ram_src_pc, ram_src_ctrl);
  or or_2 (ram_enable, ram_enable_ctrl, pc_dec7);
  Hex_Digit_Display hex_digit_display_3 (.value(display_unit_1_digit_3));  // open: dp
  Hex_Digit_Display hex_digit_display_4 (.value(display_unit_1_digit_4));  // open: dp
  Subtractor #(.width(16)) subtractor_1 (.a({rs_out, lui_data}), .b(16'h1), .out(subtractor_1_out));  // open: bin, bout
  Adder #(.width(16)) adder_1 (.a(pc_output), .b(16'h1), .out(adder_1_out));  // open: cin, cout
  ROM #(.addrWidth(16), .dataWidth(16)) rom_1 (.addr(pc_output), .data(rom_out));  // open: sel
  RAM #(.addrWidth(16), .dataWidth(16), .bus("separate")) ram_1 (
    .addr({rs_out, lui_data}), .din(ram_val), .data(ram_out), .str(ram_enable), .clk(clk));  // open: sel, ld, clr
  Multiplexer #(.select(2), .width(16), .enable("false")) multiplexer_2 (
    .in0(rt_out), .in1(zxt_imm), .in2(sxt_imm), .out(alu_inB), .sel(ALUSrcB));  // open: in3
  // Probe on ALUSrcB
  Multiplexer #(.width(16), .enable("false")) multiplexer_3 (
    .in0({rs_out, lui_data}), .in1(subtractor_1_out), .out(ram_in), .sel(ram_src));
  Multiplexer #(.width(16), .enable("false")) multiplexer_4 (
    .in0(rt_out), .in1(adder_1_out), .out(ram_val), .sel(pc_dec7));
  Multiplexer #(.width(32), .enable("false")) multiplexer_5 (
    .in0({alu_high, alu_out}), .in1(mult_and_acc), .out(prod_in), .sel(MultSrc));
  // Probe on alu_inB
  assign bit_extender_4_out = {{16{1'b0}}, alu_out};  // Bit_Extender bit_extender_4
  alu alu_1 (
    .A({rs_out, lui_data}), .B(alu_inB), .Operation(alu_oper), .Result(alu_out), .High(alu_high),
    .Zero(alu_zero), .Negative(alu_neg));
  program_counter_control program_counter_control_1 (
    .clock(clk), .Halt(halt), .Immediate(imm), .zero(zero_out), .negative(neg_out), .opcode(pc_op),
    .rd_val({rs_out, lui_data}), .rs_val({rs_out, lui_data}), .i_type(i_type), .ram_7_val(ram_out),
    .jr(jr_ctrl), .ret(ret_ctrl), .pc_out(pc_output), .pc_inc7(pc_inc7), .pc_dec7(pc_dec7),
    .ram_src_pc(ram_src_pc), .ret_cmd(ret_cmd));
  Multiplexer #(.width(3), .enable("false")) multiplexer_6 (.in0(rs_ctrl), .in1(3'b111), .out(rs), .sel(ret_cmd));
  Adder #(.width(32)) adder_2 (
    .a({mfhi_out, mflo_out}), .b(bit_extender_4_out), .out(mult_and_acc));  // open: cin, cout
  register_file register_file_1 (
    .Clock(clk), .Data(data_in), .Write_Enable(reg_en), .rd(rd), .rs(rs), .rt(rt), .incr7(inc7),
    .decr7(dec7), .I_type(i_type), .rs_out({rs_out, lui_data}), .rt_out(rt_out));
  control control_1 (
    .ROM_Input(rom_out), .halt(halt), .display_enable(display_enable), .clear_display(clear), .imm(imm),
    .data_src(DataSrc), .rd(rd), .rt(rt), .rs(rs_ctrl), .ram_write(ram_enable_ctrl),
    .ram_src_ctrl(ram_src_ctrl), .incr7(ctrl_inc7), .decr7(ctrl_dec7), .i_type(i_type), .write_en(reg_en),
    .update_fl(fl_update), .prod_en(prod_en), .mult_src(MultSrc), .alu_srcb(ALUSrcB), .alu_op(alu_oper),
    .pc_op(pc_op), .jr(jr_ctrl), .ret(ret_ctrl), .kb_enable(kbd_enable), .screen_enable(scr_enable));
  TTY tty_1 (.data(lui_data[6:0]), .clk(clk), .we(scr_enable));  // open: clr
  Register #(.width(1)) zero_register (.D(alu_zero), .en(fl_update), .Q(zero_out), .clk(clk));  // open: clr
  Register #(.width(1)) neg_register (.D(alu_neg), .en(fl_update), .Q(neg_out), .clk(clk));  // open: clr
  Register #(.width(32)) product_register (
    .D(prod_in), .en(prod_en), .Q({mfhi_out, mflo_out}), .clk(clk));  // open: clr
  or or_3 (inc7, ctrl_inc7, pc_inc7);
  or or_4 (dec7, ctrl_dec7, pc_dec7);

  // Other names for the same wires on the sheet: rs_out[7:0] = lui_data; lui_data[15:8] = imm;
  //   prod_out[31:0] = {mfhi_out, mflo_out}

  // Notes on the sheet:
  //   ROM
  //   contents of rom_1 (hex, n*v repeats v):
  //   800c 700 f818 200 900c c7d8 b810 c860 1000 b010 ffd8 a808 601 9009 1202 1a48 a03 1898 c808 640 2a00
  //   RAM
endmodule

// display
module display_unit (
  input  Clock,
  input  Clear,
  input  Write_Enable,
  input  [15:0] Data,
  output [3:0] Digit_1,
  output [3:0] Digit_2,
  output [3:0] Digit_3,
  output [3:0] Digit_4
);

  wire [15:0] data_t;

  Multiplexer #(.width(16), .enable("false")) multiplexer_1 (.in0(Data), .in1({16{1'b0}}), .out(data_t), .sel(Clear));
  Register #(.width(16), .trigger("falling")) register_1 (
    .D(data_t), .en(Write_Enable), .Q({Digit_1, Digit_2, Digit_3, Digit_4}), .clk(Clock));  // open: clr

  // Other names for the same wires on the sheet: clk = Clock; clr = Clear; data_in1[15:0] = Data
endmodule

module alu (
  input  [15:0] A,
  input  [15:0] B,
  input  [2:0] Operation,
  output [15:0] Result,
  output [15:0] High,
  output Zero,
  output Negative
);

  wire [15:0] add_out, and_out, left_out, mult_out, not_out, or_out, right_out, sub_out;

  // Probe on A
  // Probe on B
  Adder #(.width(16)) adder_1 (.a(A), .b(B), .out(add_out));  // open: cin, cout
  assign and_out = A & B;  // AND_Gate and_1, 16 bits wide
  Shifter #(.width(16)) shifter_1 (.in(A), .\dist (B[3:0]), .out(left_out));
  Subtractor #(.width(16)) subtractor_1 (.a(A), .b(B), .out(sub_out));  // open: bin, bout
  assign or_out = A | B;  // OR_Gate or_1, 16 bits wide
  Multiplexer #(.select(3), .width(16), .enable("false")) multiplexer_1 (
    .in0(add_out), .in1(sub_out), .in2(mult_out), .in3(and_out), .in4(or_out), .in5(not_out), .in6(left_out),
    .in7(right_out), .out(Result), .sel(Operation));
  Multiplier #(.width(16)) multiplier_1 (.a(A), .b(B), .out(mult_out), .cout(High));  // open: cin
  Shifter #(.width(16), .shift("lr")) shifter_2 (.in(A), .\dist (B[3:0]), .out(right_out));
  assign not_out = ~A;  // NOT_Gate not_1, 16 bits wide
  // Probe on Result
  Comparator #(.width(16)) comparator_1 (.a(Result), .b({16{1'b0}}), .eq(Zero));  // open: gt, lt
  Comparator #(.width(16)) comparator_2 (.a(Result), .b({16{1'b0}}), .lt(Negative));  // open: gt, eq

  // Other names for the same wires on the sheet: mult_high[15:0] = High; op[2:0] = Operation

  // Notes on the sheet:
  //   000 - add
  //   011 - and
  //   110 - shift left
  //   001 - sub
  //   100 - or
  //   010 - mult
  //   111 - shift right
  //   101 - not
endmodule

module register_file (
  input  Clock,
  input  [15:0] Data,
  input  Write_Enable,
  input  [2:0] rd,
  input  [2:0] rs,
  input  [2:0] rt,
  input  incr7,
  input  decr7,
  input  I_type,
  output [15:0] rs_out,
  output [15:0] rt_out
);

  wire demultiplexer_1_out7, r0en, r1en, r2en, r3en, r4en, r5en, r6en, r7en;
  wire [2:0] multiplexer_1_out;
  wire [15:0] adder_1_out, r0out, r1out, r2out, r3out, r4out, r5out, r6out, r7input, r7input2, r7out, r7out1,
       subtractor_1_out, subtractor_2_out;

  Multiplexer #(.width(3), .enable("false")) multiplexer_1 (.in0(rs), .in1(rd), .out(multiplexer_1_out), .sel(I_type));
  Multiplexer #(.select(3), .width(16), .enable("false")) multiplexer_2 (
    .in0(r0out), .in1(r1out), .in2(r2out), .in3(r3out), .in4(r4out), .in5(r5out), .in6(r6out), .in7(r7out),
    .out(rs_out), .sel(multiplexer_1_out));
  Register #(.width(16)) r0 (.D(Data), .en(r0en), .Q(r0out), .clk(Clock));  // open: clr
  Register #(.width(16)) r4 (.D(Data), .en(r4en), .Q(r4out), .clk(Clock));  // open: clr
  Multiplexer #(.select(3), .width(16), .enable("false")) multiplexer_3 (
    .in0(r0out), .in1(r1out), .in2(r2out), .in3(r3out), .in4(r4out), .in5(r5out), .in6(r6out), .in7(r7out),
    .out(rt_out), .sel(rt));
  Subtractor #(.width(16)) subtractor_1 (.a(r7out1), .b(16'h1), .out(subtractor_1_out));  // open: bin, bout
  Register #(.width(16)) r1 (.D(Data), .en(r1en), .Q(r1out), .clk(Clock));  // open: clr
  Register #(.width(16)) r5 (.D(Data), .en(r5en), .Q(r5out), .clk(Clock));  // open: clr
  Adder #(.width(16)) adder_1 (.a(r7out1), .b(16'h1), .out(adder_1_out));  // open: cin, cout
  Subtractor #(.width(16)) subtractor_2 (.a(r7out1), .b(16'h1), .out(subtractor_2_out));  // open: bin, bout
  Multiplexer #(.width(16), .enable("false")) multiplexer_4 (
    .in0(r7out1), .in1(subtractor_1_out), .out(r7out), .sel(decr7));
  Register #(.width(16)) r2 (.D(Data), .en(r2en), .Q(r2out), .clk(Clock));  // open: clr
  Register #(.width(16)) r6 (.D(Data), .en(r6en), .Q(r6out), .clk(Clock));  // open: clr
  Demultiplexer #(.select(3), .enable("false")) demultiplexer_1 (
    .out0(r0en), .out1(r1en), .out2(r2en), .out3(r3en), .out4(r4en), .out5(r5en), .out6(r6en),
    .out7(demultiplexer_1_out7), .in(Write_Enable), .sel(rd));
  Multiplexer #(.width(16), .enable("false")) multiplexer_5 (.in0(Data), .in1(adder_1_out), .out(r7input), .sel(incr7));
  Multiplexer #(.width(16), .enable("false")) multiplexer_6 (
    .in0(r7input), .in1(subtractor_2_out), .out(r7input2), .sel(decr7));
  // Probe on r7input2
  Register #(.width(16)) r3 (.D(Data), .en(r3en), .Q(r3out), .clk(Clock));  // open: clr
  Register #(.width(16)) r7 (.D(r7input2), .en(r7en), .Q(r7out1), .clk(Clock));  // open: clr
  or or_1 (r7en, incr7, demultiplexer_1_out7, decr7);

  // Other names for the same wires on the sheet: CLK = Clock; ITYPE = I_type; RSOUT[15:0] = rs_out;
  //   RTOUT[15:0] = rt_out; WRE = Write_Enable
endmodule

// pc
module program_counter_control (
  input  clock,
  input  Halt,
  input  [7:0] Immediate,
  input  zero,
  input  negative,
  input  [3:0] opcode,
  input  [15:0] rd_val,
  input  [15:0] rs_val,
  input  i_type,
  input  [15:0] ram_7_val,
  input  jr,
  input  ret,
  output [15:0] pc_out,
  output pc_inc7,
  output pc_dec7,
  output ram_src_pc,
  output ret_cmd
);

  wire b, b_out, beq, beq_out, bez, bez_out, bge, bge_out, blt, blt_out, bne, bne_out, bnz, bnz_out, halt_t,
       pc_out_choose, rd_zero;
  wire [2:0] pc_src;
  wire [15:0] imm_sxt, pc__1, pc__1_off, pc_in;

  Adder #(.width(16)) adder_1 (.a(pc_out), .b(16'h1), .out(pc__1));  // open: cin, cout
  assign imm_sxt = {{8{Immediate[7]}}, Immediate};  // Bit_Extender bit_extender_1
  Adder #(.width(16)) adder_2 (.a(pc__1), .b(imm_sxt), .out(pc__1_off));  // open: cin, cout
  not not_1 (halt_t, Halt);
  Comparator #(.width(16)) comparator_1 (.a(rd_val), .b({16{1'b0}}), .eq(rd_zero));  // open: gt, lt
  Register #(.width(16)) pc (.D(pc_in), .en(halt_t), .Q(pc_out), .clk(clock));  // open: clr
  Multiplexer #(.select(3), .width(16), .enable("false")) multiplexer_1 (
    .in0(pc__1), .in1(pc__1_off), .in2(rs_val), .in3(pc__1_off), .in4(ram_7_val), .out(pc_in), .sel(pc_src));  // open: in5, in6, in7
  Demultiplexer #(.select(4), .enable("false")) demultiplexer_1 (
    .out1(b), .out2(blt), .out3(bge), .out4(beq), .out5(bne), .out6(bez), .out7(bnz), .out8(pc_dec7),
    .in(i_type), .sel(opcode));  // open: out0, out9, out10, out11, out12, out13, out14, out15
  Priority_Encoder priority_encoder_1 (
    .in0(1'b1), .in1(pc_out_choose), .in2(jr), .in3(pc_dec7), .in4(ret), .out(pc_src));  // open: in5, in6, in7, en_in, gs, en_out
  Comparator #(.width(1)) comparator_2 (.a(b), .b(1'b1), .eq(b_out));  // open: gt, lt
  and and_1 (blt_out, blt, negative);
  and and_2 (bge_out, bge, ~negative);  // AND_Gate
  and and_3 (beq_out, beq, zero);
  and and_4 (bne_out, bne, ~zero);  // AND_Gate
  and and_5 (bez_out, bez, rd_zero);
  and and_6 (bnz_out, bnz, ~rd_zero);  // AND_Gate
  or or_1 (pc_out_choose, b_out, blt_out, bge_out, beq_out, bne_out, bez_out, bnz_out);

  assign pc_inc7 = ret;
  assign ram_src_pc = pc_dec7;
  assign ret_cmd = ret;

  // Other names for the same wires on the sheet: call = pc_dec7; clk = clock; code[3:0] = opcode;
  //   imm[7:0] = Immediate; neg = negative
endmodule

module control (
  input  [15:0] ROM_Input,
  output halt,
  output display_enable,
  output clear_display,
  output [7:0] imm,
  output [3:0] data_src,
  output [2:0] rd,
  output [2:0] rt,
  output [2:0] rs,
  output ram_write,
  output ram_src_ctrl,
  output incr7,
  output decr7,
  output i_type,
  output write_en,
  output update_fl,
  output prod_en,
  output mult_src,
  output [1:0] alu_srcb,
  output [2:0] alu_op,
  output [3:0] pc_op,
  output jr,
  output ret,
  output kb_enable,
  output screen_enable
);

  wire add, add_op, adi, \and , and_op, ani, b, beq, bez, bge, blt, bne, bnz, call, cmp, cpi, is_alu_op, ld,
       li, lui, mfhi, mflo, mov, mul, mul_op, \not , \or , or_9_out, or_10_out, or_12_out, or_op, ori, put,
       r_type, rs_src, shl, shr, sl_op, sli, sr_op, sri, st, sub, sub_op;
  wire [5:0] bit_extender_1_out;

  Demultiplexer #(.select(5), .enable("false")) demultiplexer_1 (
    .out0(halt), .out1(put), .out2(clear_display), .out3(mov), .out4(mfhi), .out5(mflo), .out6(ld),
    .out7(st), .out8(decr7), .out9(incr7), .out10(add), .out11(sub), .out12(cmp), .out13(mul),
    .out14(mult_src), .out15(\and ), .out16(\or ), .out17(\not ), .out18(shl), .out19(shr), .out20(jr),
    .out21(ret), .out22(kb_enable), .out23(screen_enable), .in(r_type), .sel(ROM_Input[13:9]));  // open: out24, out25, out26, out27, out28, out29, out30, out31
  not not_1 (r_type, ROM_Input[15]);
  or or_1 (prod_en, mul, mult_src);
  or or_2 (add_op, add, adi);
  or or_3 (sub_op, sub, cmp, cpi);
  or or_4 (mul_op, mul, mult_src);
  or or_5 (and_op, \and , ani);
  or or_6 (or_op, \or , ori);
  or or_7 (sl_op, shl, sli);
  or or_8 (sr_op, shr, sri);
  Demultiplexer #(.select(4), .enable("false")) demultiplexer_2 (
    .out0(li), .out1(lui), .out2(adi), .out3(ani), .out4(ori), .out5(sli), .out6(sri), .out7(cpi), .out8(b),
    .out9(blt), .out10(bge), .out11(beq), .out12(bne), .out13(bez), .out14(bnz), .out15(call),
    .in(ROM_Input[15]), .sel(ROM_Input[14:11]));
  or or_9 (or_9_out, ani, ori, sli, sri);
  or or_10 (or_10_out, adi, cpi);
  assign bit_extender_1_out = {{2{1'b0}}, ROM_Input[14:11]};  // Bit_Extender bit_extender_1
  or or_11 (is_alu_op, add, sub, cmp, \and , \or , \not , shl, shr, adi, ani, ori, sli, sri, cpi);
  Multiplexer #(.width(6), .enable("false")) multiplexer_1 (
    .in0(ROM_Input[14:9]), .in1(bit_extender_1_out), .sel(ROM_Input[15]));  // open: out
  or or_12 (or_12_out, ld, incr7);
  Priority_Encoder #(.select(2)) priority_encoder_1 (
    .in0(1'b1), .in1(or_9_out), .in2(or_10_out), .out(alu_srcb));  // open: in3, gs, en_out, en_in
  Priority_Encoder #(.select(4)) priority_encoder_2 (
    .in0(1'b1), .in1(li), .in2(lui), .in3(mov), .in4(mfhi), .in5(mflo), .in6(or_12_out), .in7(is_alu_op),
    .in8(kb_enable), .out(data_src));  // open: in9, in10, in11, in12, in13, in14, in15, gs, en_out, en_in
  Multiplexer #(.width(3), .enable("false")) multiplexer_2 (.in0(ROM_Input[8:6]), .in1(3'b111), .out(rs), .sel(rs_src));
  Priority_Encoder priority_encoder_3 (
    .in0(add_op), .in1(sub_op), .in2(mul_op), .in3(and_op), .in4(or_op), .in5(\not ), .in6(sl_op),
    .in7(sr_op), .out(alu_op));  // open: en_in, gs, en_out
  or or_13 (ram_write, st, decr7);
  or or_14 (rs_src, incr7, decr7);
  or or_15 (update_fl, add, sub, cmp, adi, cpi);
  and and_1 (write_en, ~cmp, ~cpi, ~mul, ~mult_src);  // AND_Gate
  or or_16 (display_enable, put, clear_display);
  Priority_Encoder #(.select(4)) priority_encoder_4 (
    .in0(1'b1), .in1(b), .in2(blt), .in3(bge), .in4(beq), .in5(bne), .in6(bez), .in7(bnz), .in8(call),
    .out(pc_op));  // open: in9, in10, in11, in12, in13, in14, in15, gs, en_out, en_in
  Multiplexer #(.width(3), .enable("false")) multiplexer_3 (.in0(ROM_Input[2:0]), .in1(3'b111), .out(rd), .sel(call));

  assign i_type = ROM_Input[15];
  assign imm = ROM_Input[10:3];
  assign ram_src_ctrl = decr7;
  assign rt = ROM_Input[5:3];

  // Other names for the same wires on the sheet: clr = clear_display; in = kb_enable; mac = mult_src; not_op = \not ;
  //   out = screen_enable; pop = incr7; push = decr7; rd_out[2:0] = ROM_Input[2:0]; rs_out[2:0] = ROM_Input[8:6];
  //   opcode_r[5:0] = ROM_Input[14:9]; opcode_i[3:0] = ROM_Input[14:11]

  // Notes on the sheet:
  //   r-type
  //   i-type
endmodule
