// Logisim project jaw280_lab7.circ as structural Verilog: 1 circuit, main circuit main
module main (
);

  wire button_1_out, CLK, clock_1_out, comparator_2_eq, Done, not_1_out, not_2_out, not_3_out, Write;
  wire [7:0] Multiplier_q, shifter_2_out;
  wire [15:0] adder_1_out, Multiplicand_q, Product_q, shifter_1_out;

  Clock clock_1 (.out(clock_1_out));
  Button button_1 (.out(button_1_out));
  LED u_Done (.in(Done));
  or or_1 (CLK, clock_1_out, button_1_out);
  Shifter #(.width(16)) shifter_1 (.in(Multiplicand_q), .\dist (4'b0001), .out(shifter_1_out));
  not not_1 (not_1_out, Done);
  // Probe on Multiplicand_q
  Register #(.width(16)) Multiplicand (.D(shifter_1_out), .en(not_1_out), .Q(Multiplicand_q), .clk(CLK));  // open: clr
  Register #(.width(16)) Product (.D(adder_1_out), .en(Write), .Q(Product_q), .clk(CLK));  // open: clr
  // Probe on Product_q
  Shifter #(.shift("lr")) shifter_2 (.in(Multiplier_q), .\dist (3'b001), .out(shifter_2_out));
  Adder #(.width(16)) adder_1 (.a(Multiplicand_q), .b(Product_q), .out(adder_1_out));  // open: cin, cout
  // Probe on Multiplier_q
  Register Multiplier (.D(shifter_2_out), .Q(Multiplier_q), .clk(CLK));  // open: en, clr
  Comparator comparator_1 (.a(Multiplier_q), .b({8{1'b0}}), .eq(Done));  // open: gt, lt
  Comparator #(.width(1)) comparator_2 (.a(Multiplier_q[0]), .b(1'b0), .eq(comparator_2_eq));  // open: gt, lt
  not not_2 (not_2_out, Done);
  not not_3 (not_3_out, comparator_2_eq);
  and and_1 (Write, not_3_out, not_2_out);
endmodule
