// Logisim project jaw280_lab8.circ as structural Verilog: 2 circuits, main circuit main
module main (
);

  Register_File register_file_1 ();  // open: Clock, Data, Write_Enable, rd, rs, rt, incr7, decr7, rs_out, rt_out
endmodule

module Register_File (
  input  Clock,
  input  [15:0] Data,
  input  Write_Enable,
  input  [2:0] rd,
  input  [2:0] rs,
  input  [2:0] rt,
  input  incr7,
  input  decr7,
  output [15:0] rs_out,
  output [15:0] rt_out
);

  wire demultiplexer_1_out7, r0en, r1en, r2en, r3en, r4en, r5en, r6en, r7en;
  wire [15:0] adder_1_out, r0out, r1out, r2out, r3out, r4out, r5out, r6out, r7input, r7input2, r7out, r7out1,
       subtractor_1_out, subtractor_2_out;

  Multiplexer #(.select(3), .width(16), .enable("false")) multiplexer_1 (
    .in0(r0out), .in1(r1out), .in2(r2out), .in3(r3out), .in4(r4out), .in5(r5out), .in6(r6out), .in7(r7out),
    .out(rs_out), .sel(rs));
  Register #(.width(16)) r0 (.D(Data), .en(r0en), .Q(r0out), .clk(Clock));  // open: clr
  Register #(.width(16)) r4 (.D(Data), .en(r4en), .Q(r4out), .clk(Clock));  // open: clr
  Multiplexer #(.select(3), .width(16), .enable("false")) multiplexer_2 (
    .in0(r0out), .in1(r1out), .in2(r2out), .in3(r3out), .in4(r4out), .in5(r5out), .in6(r6out), .in7(r7out),
    .out(rt_out), .sel(rt));
  Subtractor #(.width(16)) subtractor_1 (.a(r7out1), .b(16'h1), .out(subtractor_1_out));  // open: bin, bout
  Register #(.width(16)) r1 (.D(Data), .en(r1en), .Q(r1out), .clk(Clock));  // open: clr
  Register #(.width(16)) r5 (.D(Data), .en(r5en), .Q(r5out), .clk(Clock));  // open: clr
  Adder #(.width(16)) adder_1 (.a(r7out1), .b(16'h1), .out(adder_1_out));  // open: cin, cout
  Subtractor #(.width(16)) subtractor_2 (.a(r7out1), .b(16'h1), .out(subtractor_2_out));  // open: bin, bout
  Multiplexer #(.width(16), .enable("false")) multiplexer_3 (
    .in0(r7out1), .in1(subtractor_1_out), .out(r7out), .sel(decr7));
  Register #(.width(16)) r2 (.D(Data), .en(r2en), .Q(r2out), .clk(Clock));  // open: clr
  Register #(.width(16)) r6 (.D(Data), .en(r6en), .Q(r6out), .clk(Clock));  // open: clr
  Demultiplexer #(.select(3), .enable("false")) demultiplexer_1 (
    .out0(r0en), .out1(r1en), .out2(r2en), .out3(r3en), .out4(r4en), .out5(r5en), .out6(r6en),
    .out7(demultiplexer_1_out7), .in(Write_Enable), .sel(rd));
  Multiplexer #(.width(16), .enable("false")) multiplexer_4 (.in0(Data), .in1(adder_1_out), .out(r7input), .sel(incr7));
  Multiplexer #(.width(16), .enable("false")) multiplexer_5 (
    .in0(r7input), .in1(subtractor_2_out), .out(r7input2), .sel(decr7));
  // Probe on r7input2
  Register #(.width(16)) r3 (.D(Data), .en(r3en), .Q(r3out), .clk(Clock));  // open: clr
  Register #(.width(16)) r7 (.D(r7input2), .en(r7en), .Q(r7out1), .clk(Clock));  // open: clr
  or or_1 (r7en, incr7, demultiplexer_1_out7, decr7);

  // Other names for the same wires on the sheet: CLK = Clock; RSOUT[15:0] = rs_out; RTOUT[15:0] = rt_out;
  //   WRE = Write_Enable
endmodule
